# Fritzing sketch circuit (saved by Fritzing 0.8.7b)
breadboards: 1

parts:
  Part1 = Arduino Mega 2560 (Rev3)
  LCD1 = LCD screen
  R2 = Rotary Potentiometer (Small) [maximum_resistance=10kΩ package=THT]
  LED1 = LEDs [package=led10mm]
  LED2 = LEDs [package=led10mm]
  SG7 = Buzzer 12mm [package=buzzer-ccv]
  R4 = Resistor [package="2010 [SMD]"]
  Part3 = RFID-RC522-v2
  SG8 = Buzzer 12mm [package=buzzer-ccv]  # not connected
  SG9 = Buzzer 12mm [package=buzzer-12mm]  # not connected
  Part4 = LilyPad Buzzer  # not connected
  SG10 = Buzzer 12mm [package=buzzer-ccv]  # not connected
  Matrix_keypad2 = KEYPAD 4x4

nets:
  N1: Part1.D12_PWM, LCD1.RS
  N2: Part1.D11_PWM, LCD1.E
  N3: Part1.D10_PWM, Part3.RST
  N4: Part1.3V3, Part3.3_3V
  5V: Part1.5V, LCD1.VDD, R2.leg1, R4.Pin_0
  GND: Part1.GND, LCD1.VSS, LCD1.R/W, LCD1.LED-, R2.leg2, LED1.A, LED2.C, SG7.1, Part3.GND
  N5: Part1.D22, LED1.C
  N6: Part1.D25, LED2.A
  N7: Part1.D26, Matrix_keypad2.col1
  N8: Part1.D28, Matrix_keypad2.col2
  N9: Part1.D30, Matrix_keypad2.col3
  N10: Part1.D32, Matrix_keypad2.col4
  N11: Part1.D34, Matrix_keypad2.row1
  N12: Part1.D36, Matrix_keypad2.row2
  N13: Part1.D38, Matrix_keypad2.row3
  N14: Part1.D40, Matrix_keypad2.row4
  N15: Part1.D50, Part3.MISO
  N16: Part1.D51, Part3.MOSI
  N17: Part1.D52, Part3.SCK
  N18: Part1.D53, Part3.SDA
  N19: LCD1.V0, R2.wiper
  N20: LCD1.LED+, R4.Pin_1

custom parts:
  Resistor: Resistor Basic schematic elements and footprints for 0603, 1206, and PTH resistors.
  RFID-RC522-v2: A simple China made RFID-RC522 Reader; do check the pin labels, as this is a MFRC522 based clone.
  KEYPAD 4x4: Matrix keypad 16 buttons, 4 rows x 4 columns
